# Fritzing sketch BoardLightDetector (saved by Fritzing 0.9.2b)
breadboards: 1

parts:
  U1 = NodeMCU V1.0
  R1 = Resistor [tolerance=±5% resistance=220 package="0603 [SMD]"]
  R2 = PHOTOCELL [package=photocell-kit]
  LED1 = smd LED [color="Red (633nm)" package="0603 [SMD]"]

nets:
  N1: U1.D7, LED1.anode
  N2: U1.GND, R2.P$2, LED1.cathode
  N3: U1.3V3, R1.Pin_0
  N4: U1.A0, R1.Pin_1, R2.P$1

custom parts:
  NodeMCU V1.0: ESP9266 based NodeMCU
